// Logisim project Banco de Registradores.circ as structural Verilog: 2 circuits, main circuit Registrador
module Registrador (
  input  [31:0] DataIn,
  input  Write,
  output [31:0] DataIn_2
);

  D_Flip_Flop d_ff_1 (.clk(Write), .D(DataIn[31]), .Q(DataIn_2[31]));  // open: Qn, preset, en, reset
  D_Flip_Flop d_ff_2 (.clk(Write), .D(DataIn[30]), .Q(DataIn_2[30]));  // open: Qn, preset, en, reset
  D_Flip_Flop d_ff_3 (.clk(Write), .D(DataIn[29]), .Q(DataIn_2[29]));  // open: Qn, preset, en, reset
  D_Flip_Flop d_ff_4 (.clk(Write), .D(DataIn[28]), .Q(DataIn_2[28]));  // open: Qn, preset, en, reset
  D_Flip_Flop d_ff_5 (.clk(Write), .D(DataIn[27]), .Q(DataIn_2[27]));  // open: Qn, preset, en, reset
  D_Flip_Flop d_ff_6 (.clk(Write), .D(DataIn[26]), .Q(DataIn_2[26]));  // open: Qn, preset, en, reset
  D_Flip_Flop d_ff_7 (.clk(Write), .D(DataIn[25]), .Q(DataIn_2[25]));  // open: Qn, preset, en, reset
  D_Flip_Flop d_ff_8 (.clk(Write), .D(DataIn[24]), .Q(DataIn_2[24]));  // open: Qn, preset, en, reset
  D_Flip_Flop d_ff_9 (.clk(Write), .D(DataIn[23]), .Q(DataIn_2[23]));  // open: Qn, preset, en, reset
  D_Flip_Flop d_ff_10 (.clk(Write), .D(DataIn[22]), .Q(DataIn_2[22]));  // open: Qn, preset, en, reset
  D_Flip_Flop d_ff_11 (.clk(Write), .D(DataIn[21]), .Q(DataIn_2[21]));  // open: Qn, preset, en, reset
  D_Flip_Flop d_ff_12 (.clk(Write), .D(DataIn[20]), .Q(DataIn_2[20]));  // open: Qn, preset, en, reset
  D_Flip_Flop d_ff_13 (.clk(Write), .D(DataIn[19]), .Q(DataIn_2[19]));  // open: Qn, preset, en, reset
  D_Flip_Flop d_ff_14 (.clk(Write), .D(DataIn[18]), .Q(DataIn_2[18]));  // open: Qn, preset, en, reset
  D_Flip_Flop d_ff_15 (.clk(Write), .D(DataIn[17]), .Q(DataIn_2[17]));  // open: Qn, preset, en, reset
  D_Flip_Flop d_ff_16 (.clk(Write), .D(DataIn[16]), .Q(DataIn_2[16]));  // open: Qn, preset, en, reset
  D_Flip_Flop d_ff_17 (.clk(Write), .D(DataIn[15]), .Q(DataIn_2[15]));  // open: Qn, preset, en, reset
  D_Flip_Flop d_ff_18 (.clk(Write), .D(DataIn[14]), .Q(DataIn_2[14]));  // open: Qn, preset, en, reset
  D_Flip_Flop d_ff_19 (.clk(Write), .D(DataIn[13]), .Q(DataIn_2[13]));  // open: Qn, preset, en, reset
  D_Flip_Flop d_ff_20 (.clk(Write), .D(DataIn[12]), .Q(DataIn_2[12]));  // open: Qn, preset, en, reset
  D_Flip_Flop d_ff_21 (.clk(Write), .D(DataIn[11]), .Q(DataIn_2[11]));  // open: Qn, preset, en, reset
  D_Flip_Flop d_ff_22 (.clk(Write), .D(DataIn[10]), .Q(DataIn_2[10]));  // open: Qn, preset, en, reset
  D_Flip_Flop d_ff_23 (.clk(Write), .D(DataIn[9]), .Q(DataIn_2[9]));  // open: Qn, preset, en, reset
  D_Flip_Flop d_ff_24 (.clk(Write), .D(DataIn[8]), .Q(DataIn_2[8]));  // open: Qn, preset, en, reset
  D_Flip_Flop d_ff_25 (.clk(Write), .D(DataIn[7]), .Q(DataIn_2[7]));  // open: Qn, preset, en, reset
  D_Flip_Flop d_ff_26 (.clk(Write), .D(DataIn[6]), .Q(DataIn_2[6]));  // open: Qn, preset, en, reset
  D_Flip_Flop d_ff_27 (.clk(Write), .D(DataIn[5]), .Q(DataIn_2[5]));  // open: Qn, preset, en, reset
  D_Flip_Flop d_ff_28 (.clk(Write), .D(DataIn[4]), .Q(DataIn_2[4]));  // open: Qn, preset, en, reset
  D_Flip_Flop d_ff_29 (.clk(Write), .D(DataIn[3]), .Q(DataIn_2[3]));  // open: Qn, preset, en, reset
  D_Flip_Flop d_ff_30 (.clk(Write), .D(DataIn[2]), .Q(DataIn_2[2]));  // open: Qn, preset, en, reset
  D_Flip_Flop d_ff_31 (.clk(Write), .D(DataIn[1]), .Q(DataIn_2[1]));  // open: Qn, preset, en, reset
  D_Flip_Flop d_ff_32 (.clk(Write), .D(DataIn[0]), .Q(DataIn_2[0]));  // open: Qn, preset, en, reset
endmodule

module Banco_de_Registradores (
  input  [31:0] DataIn,
  input  [4:0] Sel_Write,
  input  [4:0] Sel_Rx,
  input  Write,
  input  [4:0] Sel_Ry,
  output [31:0] Rx,
  output [31:0] Ry,
  output [31:0] Rw
);

  wire demultiplexer_1_out0, demultiplexer_1_out1, demultiplexer_1_out2, demultiplexer_1_out3,
       demultiplexer_1_out4, demultiplexer_1_out5, demultiplexer_1_out6, demultiplexer_1_out7,
       demultiplexer_1_out8, demultiplexer_1_out9, demultiplexer_1_out10, demultiplexer_1_out11,
       demultiplexer_1_out12, demultiplexer_1_out13, demultiplexer_1_out14, demultiplexer_1_out15,
       demultiplexer_1_out16, demultiplexer_1_out17, demultiplexer_1_out18, demultiplexer_1_out19,
       demultiplexer_1_out20, demultiplexer_1_out21, demultiplexer_1_out22, demultiplexer_1_out23,
       demultiplexer_1_out24, demultiplexer_1_out25, demultiplexer_1_out26, demultiplexer_1_out27,
       demultiplexer_1_out28, demultiplexer_1_out29, demultiplexer_1_out30, demultiplexer_1_out31;
  wire [31:0] registrador_1_datain_2, registrador_2_datain_2, registrador_3_datain_2, registrador_4_datain_2,
       registrador_5_datain_2, registrador_6_datain_2, registrador_7_datain_2, registrador_8_datain_2,
       registrador_9_datain_2, registrador_10_datain_2, registrador_11_datain_2, registrador_12_datain_2,
       registrador_13_datain_2, registrador_14_datain_2, registrador_15_datain_2, registrador_16_datain_2,
       registrador_17_datain_2, registrador_18_datain_2, registrador_19_datain_2, registrador_20_datain_2,
       registrador_21_datain_2, registrador_22_datain_2, registrador_23_datain_2, registrador_24_datain_2,
       registrador_25_datain_2, registrador_26_datain_2, registrador_27_datain_2, registrador_28_datain_2,
       registrador_29_datain_2, registrador_30_datain_2, registrador_31_datain_2, registrador_32_datain_2;

  Demultiplexer #(.select(5), .enable("false")) demultiplexer_1 (
    .out0(demultiplexer_1_out0), .out1(demultiplexer_1_out1), .out2(demultiplexer_1_out2),
    .out3(demultiplexer_1_out3), .out4(demultiplexer_1_out4), .out5(demultiplexer_1_out5),
    .out6(demultiplexer_1_out6), .out7(demultiplexer_1_out7), .out8(demultiplexer_1_out8),
    .out9(demultiplexer_1_out9), .out10(demultiplexer_1_out10), .out11(demultiplexer_1_out11),
    .out12(demultiplexer_1_out12), .out13(demultiplexer_1_out13), .out14(demultiplexer_1_out14),
    .out15(demultiplexer_1_out15), .out16(demultiplexer_1_out16), .out17(demultiplexer_1_out17),
    .out18(demultiplexer_1_out18), .out19(demultiplexer_1_out19), .out20(demultiplexer_1_out20),
    .out21(demultiplexer_1_out21), .out22(demultiplexer_1_out22), .out23(demultiplexer_1_out23),
    .out24(demultiplexer_1_out24), .out25(demultiplexer_1_out25), .out26(demultiplexer_1_out26),
    .out27(demultiplexer_1_out27), .out28(demultiplexer_1_out28), .out29(demultiplexer_1_out29),
    .out30(demultiplexer_1_out30), .out31(demultiplexer_1_out31), .in(Write), .sel(Sel_Write));
  Registrador registrador_1 (.Write(demultiplexer_1_out0), .DataIn(DataIn), .DataIn_2(registrador_1_datain_2));
  Registrador registrador_2 (.Write(demultiplexer_1_out1), .DataIn(DataIn), .DataIn_2(registrador_2_datain_2));
  Registrador registrador_3 (.Write(demultiplexer_1_out2), .DataIn(DataIn), .DataIn_2(registrador_3_datain_2));
  Registrador registrador_4 (.Write(demultiplexer_1_out3), .DataIn(DataIn), .DataIn_2(registrador_4_datain_2));
  Registrador registrador_5 (.Write(demultiplexer_1_out4), .DataIn(DataIn), .DataIn_2(registrador_5_datain_2));
  Registrador registrador_6 (.Write(demultiplexer_1_out5), .DataIn(DataIn), .DataIn_2(registrador_6_datain_2));
  Registrador registrador_7 (.Write(demultiplexer_1_out6), .DataIn(DataIn), .DataIn_2(registrador_7_datain_2));
  Registrador registrador_8 (.Write(demultiplexer_1_out7), .DataIn(DataIn), .DataIn_2(registrador_8_datain_2));
  Registrador registrador_9 (.Write(demultiplexer_1_out8), .DataIn(DataIn), .DataIn_2(registrador_9_datain_2));
  Registrador registrador_10 (.Write(demultiplexer_1_out9), .DataIn(DataIn), .DataIn_2(registrador_10_datain_2));
  Registrador registrador_11 (.Write(demultiplexer_1_out10), .DataIn(DataIn), .DataIn_2(registrador_11_datain_2));
  Registrador registrador_12 (.Write(demultiplexer_1_out11), .DataIn(DataIn), .DataIn_2(registrador_12_datain_2));
  Registrador registrador_13 (.Write(demultiplexer_1_out12), .DataIn(DataIn), .DataIn_2(registrador_13_datain_2));
  Registrador registrador_14 (.Write(demultiplexer_1_out13), .DataIn(DataIn), .DataIn_2(registrador_14_datain_2));
  Registrador registrador_15 (.Write(demultiplexer_1_out14), .DataIn(DataIn), .DataIn_2(registrador_15_datain_2));
  Registrador registrador_16 (.Write(demultiplexer_1_out15), .DataIn(DataIn), .DataIn_2(registrador_16_datain_2));
  Registrador registrador_17 (.Write(demultiplexer_1_out16), .DataIn(DataIn), .DataIn_2(registrador_17_datain_2));
  Registrador registrador_18 (.Write(demultiplexer_1_out17), .DataIn(DataIn), .DataIn_2(registrador_18_datain_2));
  Registrador registrador_19 (.Write(demultiplexer_1_out18), .DataIn(DataIn), .DataIn_2(registrador_19_datain_2));
  Registrador registrador_20 (.Write(demultiplexer_1_out19), .DataIn(DataIn), .DataIn_2(registrador_20_datain_2));
  Registrador registrador_21 (.Write(demultiplexer_1_out20), .DataIn(DataIn), .DataIn_2(registrador_21_datain_2));
  Registrador registrador_22 (.Write(demultiplexer_1_out21), .DataIn(DataIn), .DataIn_2(registrador_22_datain_2));
  Registrador registrador_23 (.Write(demultiplexer_1_out22), .DataIn(DataIn), .DataIn_2(registrador_23_datain_2));
  Registrador registrador_24 (.Write(demultiplexer_1_out23), .DataIn(DataIn), .DataIn_2(registrador_24_datain_2));
  Registrador registrador_25 (.Write(demultiplexer_1_out24), .DataIn(DataIn), .DataIn_2(registrador_25_datain_2));
  Registrador registrador_26 (.Write(demultiplexer_1_out25), .DataIn(DataIn), .DataIn_2(registrador_26_datain_2));
  Registrador registrador_27 (.Write(demultiplexer_1_out26), .DataIn(DataIn), .DataIn_2(registrador_27_datain_2));
  Registrador registrador_28 (.Write(demultiplexer_1_out27), .DataIn(DataIn), .DataIn_2(registrador_28_datain_2));
  Registrador registrador_29 (.Write(demultiplexer_1_out28), .DataIn(DataIn), .DataIn_2(registrador_29_datain_2));
  Registrador registrador_30 (.Write(demultiplexer_1_out29), .DataIn(DataIn), .DataIn_2(registrador_30_datain_2));
  Registrador registrador_31 (.Write(demultiplexer_1_out30), .DataIn(DataIn), .DataIn_2(registrador_31_datain_2));
  Registrador registrador_32 (.Write(demultiplexer_1_out31), .DataIn(DataIn), .DataIn_2(registrador_32_datain_2));
  Multiplexer #(.select(5), .width(32), .enable("false")) multiplexer_1 (
    .in0(registrador_1_datain_2), .in1(registrador_2_datain_2), .in2(registrador_3_datain_2),
    .in3(registrador_4_datain_2), .in4(registrador_5_datain_2), .in5(registrador_6_datain_2),
    .in6(registrador_7_datain_2), .in7(registrador_8_datain_2), .in8(registrador_9_datain_2),
    .in9(registrador_10_datain_2), .in10(registrador_11_datain_2), .in11(registrador_12_datain_2),
    .in12(registrador_13_datain_2), .in13(registrador_14_datain_2), .in14(registrador_15_datain_2),
    .in15(registrador_16_datain_2), .in16(registrador_17_datain_2), .in17(registrador_18_datain_2),
    .in18(registrador_19_datain_2), .in19(registrador_20_datain_2), .in20(registrador_21_datain_2),
    .in21(registrador_22_datain_2), .in22(registrador_23_datain_2), .in23(registrador_24_datain_2),
    .in24(registrador_25_datain_2), .in25(registrador_26_datain_2), .in26(registrador_27_datain_2),
    .in27(registrador_28_datain_2), .in28(registrador_29_datain_2), .in29(registrador_30_datain_2),
    .in30(registrador_31_datain_2), .in31(registrador_32_datain_2), .out(Rx), .sel(Sel_Rx));
  Multiplexer #(.select(5), .width(32), .enable("false")) multiplexer_2 (
    .in0(registrador_1_datain_2), .in1(registrador_2_datain_2), .in2(registrador_3_datain_2),
    .in3(registrador_4_datain_2), .in4(registrador_5_datain_2), .in5(registrador_6_datain_2),
    .in6(registrador_7_datain_2), .in7(registrador_8_datain_2), .in8(registrador_9_datain_2),
    .in9(registrador_10_datain_2), .in10(registrador_11_datain_2), .in11(registrador_12_datain_2),
    .in12(registrador_13_datain_2), .in13(registrador_14_datain_2), .in14(registrador_15_datain_2),
    .in15(registrador_16_datain_2), .in16(registrador_17_datain_2), .in17(registrador_18_datain_2),
    .in18(registrador_19_datain_2), .in19(registrador_20_datain_2), .in20(registrador_21_datain_2),
    .in21(registrador_22_datain_2), .in22(registrador_23_datain_2), .in23(registrador_24_datain_2),
    .in24(registrador_25_datain_2), .in25(registrador_26_datain_2), .in26(registrador_27_datain_2),
    .in27(registrador_28_datain_2), .in28(registrador_29_datain_2), .in29(registrador_30_datain_2),
    .in30(registrador_31_datain_2), .in31(registrador_32_datain_2), .out(Ry), .sel(Sel_Ry));
  Multiplexer #(.select(5), .width(32), .enable("false")) multiplexer_3 (
    .in0(registrador_1_datain_2), .in1(registrador_2_datain_2), .in2(registrador_3_datain_2),
    .in3(registrador_4_datain_2), .in4(registrador_5_datain_2), .in5(registrador_6_datain_2),
    .in6(registrador_7_datain_2), .in7(registrador_8_datain_2), .in8(registrador_9_datain_2),
    .in9(registrador_10_datain_2), .in10(registrador_11_datain_2), .in11(registrador_12_datain_2),
    .in12(registrador_13_datain_2), .in13(registrador_14_datain_2), .in14(registrador_15_datain_2),
    .in15(registrador_16_datain_2), .in16(registrador_17_datain_2), .in17(registrador_18_datain_2),
    .in18(registrador_19_datain_2), .in19(registrador_20_datain_2), .in20(registrador_21_datain_2),
    .in21(registrador_22_datain_2), .in22(registrador_23_datain_2), .in23(registrador_24_datain_2),
    .in24(registrador_25_datain_2), .in25(registrador_26_datain_2), .in26(registrador_27_datain_2),
    .in27(registrador_28_datain_2), .in28(registrador_29_datain_2), .in29(registrador_30_datain_2),
    .in30(registrador_31_datain_2), .in31(registrador_32_datain_2), .out(Rw), .sel(Sel_Write));
endmodule
