// Logisim project Display.circ as structural Verilog: 4 circuits, main circuit display
module display (
  input  [31:0] in_1
);

  wire [3:0] display_5_2_1__0, display_5_2_1__1, display_12_4_1__0, display_12_4_1__1, display_12_4_1__2,
       display_12_4_1__3, display_32_9_1__0, display_32_9_1__1, display_32_9_1__2, display_32_9_1__3,
       display_32_9_1__4, display_32_9_1__5, display_32_9_1__6, display_32_9_1__7, display_32_9_1__8,
       display_32_9_1__9;
  wire [31:0] divider_1_out, divider_1_rem, divider_2_out, divider_2_rem, divider_3_out, divider_3_rem,
       divider_4_out, divider_4_rem, divider_5_out, divider_5_rem, divider_6_out, divider_6_rem,
       divider_7_out, divider_7_rem, divider_8_rem, divider_9_out, divider_9_rem, divider_10_out,
       divider_10_rem;

  Hex_Digit_Display hex_digit_display_1 (.value(display_12_4_1__3));  // open: dp
  Hex_Digit_Display hex_digit_display_2 (.value(display_5_2_1__1));  // open: dp
  Hex_Digit_Display hex_digit_display_3 (.value(display_12_4_1__1));  // open: dp
  Hex_Digit_Display hex_digit_display_4 (.value(display_12_4_1__2));  // open: dp
  Display_12___4 display_12_4_1 (
    ._0(display_12_4_1__0), ._1(display_12_4_1__1), ._2(display_12_4_1__2), ._3(display_12_4_1__3));  // open: in_1
  Hex_Digit_Display hex_digit_display_5 (.value(display_5_2_1__0));  // open: dp
  Display_5___2 display_5_2_1 (._0(display_5_2_1__0), ._1(display_5_2_1__1));  // open: in_1
  Hex_Digit_Display hex_digit_display_6 (.value(display_12_4_1__0));  // open: dp
  Divider #(.width(32)) divider_1 (
    .a(divider_10_out), .b(32'ha), .out(divider_1_out), .rem(divider_1_rem));  // open: upper
  Divider #(.width(32)) divider_2 (
    .a(divider_1_out), .b(32'ha), .out(divider_2_out), .rem(divider_2_rem));  // open: upper
  Divider #(.width(32)) divider_3 (
    .a(divider_2_out), .b(32'ha), .out(divider_3_out), .rem(divider_3_rem));  // open: upper
  Divider #(.width(32)) divider_4 (
    .a(divider_3_out), .b(32'ha), .out(divider_4_out), .rem(divider_4_rem));  // open: upper
  Divider #(.width(32)) divider_5 (
    .a(divider_4_out), .b(32'ha), .out(divider_5_out), .rem(divider_5_rem));  // open: upper
  Divider #(.width(32)) divider_6 (
    .a(divider_5_out), .b(32'ha), .out(divider_6_out), .rem(divider_6_rem));  // open: upper
  Divider #(.width(32)) divider_7 (
    .a(divider_6_out), .b(32'ha), .out(divider_7_out), .rem(divider_7_rem));  // open: upper
  Divider #(.width(32)) divider_8 (.a(divider_7_out), .b(32'ha), .rem(divider_8_rem));  // open: out, upper
  Divider #(.width(32)) divider_9 (.a(in_1), .b(32'ha), .out(divider_9_out), .rem(divider_9_rem));  // open: upper
  Divider #(.width(32)) divider_10 (
    .a(divider_9_out), .b(32'ha), .out(divider_10_out), .rem(divider_10_rem));  // open: upper
  Hex_Digit_Display hex_digit_display_7 (.value(divider_8_rem[3:0]));  // open: dp
  Hex_Digit_Display hex_digit_display_8 (.value(divider_7_rem[3:0]));  // open: dp
  Hex_Digit_Display hex_digit_display_9 (.value(divider_6_rem[3:0]));  // open: dp
  Hex_Digit_Display hex_digit_display_10 (.value(divider_5_rem[3:0]));  // open: dp
  Hex_Digit_Display hex_digit_display_11 (.value(divider_4_rem[3:0]));  // open: dp
  Hex_Digit_Display hex_digit_display_12 (.value(divider_2_rem[3:0]));  // open: dp
  Hex_Digit_Display hex_digit_display_13 (.value(divider_3_rem[3:0]));  // open: dp
  Hex_Digit_Display hex_digit_display_14 (.value(divider_1_rem[3:0]));  // open: dp
  Hex_Digit_Display hex_digit_display_15 (.value(divider_10_rem[3:0]));  // open: dp
  Hex_Digit_Display hex_digit_display_16 (.value(divider_9_rem[3:0]));  // open: dp
  Hex_Digit_Display hex_digit_display_17 (.value(display_32_9_1__9));  // open: dp
  Hex_Digit_Display hex_digit_display_18 (.value(display_32_9_1__8));  // open: dp
  Hex_Digit_Display hex_digit_display_19 (.value(display_32_9_1__6));  // open: dp
  Hex_Digit_Display hex_digit_display_20 (.value(display_32_9_1__7));  // open: dp
  Hex_Digit_Display hex_digit_display_21 (.value(display_32_9_1__4));  // open: dp
  Hex_Digit_Display hex_digit_display_22 (.value(display_32_9_1__5));  // open: dp
  Display_32___9 display_32_9_1 (
    ._0(display_32_9_1__0), ._1(display_32_9_1__1), ._2(display_32_9_1__2), ._3(display_32_9_1__3),
    ._4(display_32_9_1__4), ._5(display_32_9_1__5), ._6(display_32_9_1__6), ._7(display_32_9_1__7),
    ._8(display_32_9_1__8), ._9(display_32_9_1__9));  // open: in_1
  Hex_Digit_Display hex_digit_display_23 (.value(display_32_9_1__3));  // open: dp
  Hex_Digit_Display hex_digit_display_24 (.value(display_32_9_1__2));  // open: dp
  Hex_Digit_Display hex_digit_display_25 (.value(display_32_9_1__1));  // open: dp
  Hex_Digit_Display hex_digit_display_26 (.value(display_32_9_1__0));  // open: dp
endmodule

module Display_32___9 (
  input  [31:0] in_1,
  output [3:0] _0,
  output [3:0] _1,
  output [3:0] _2,
  output [3:0] _3,
  output [3:0] _4,
  output [3:0] _5,
  output [3:0] _6,
  output [3:0] _7,
  output [3:0] _8,
  output [3:0] _9
);

  wire [31:0] divider_1_out, divider_2_out, divider_3_out, divider_4_out, divider_5_out, divider_6_out,
       divider_7_out, divider_9_out, divider_10_out;
  wire [31:4] divider_1_rem, divider_2_rem, divider_3_rem, divider_4_rem, divider_5_rem, divider_6_rem,
       divider_7_rem, divider_8_rem, divider_9_rem, divider_10_rem;

  Divider #(.width(32)) divider_1 (
    .a(divider_10_out), .b(32'ha), .out(divider_1_out), .rem({divider_1_rem, _2}));  // open: upper
  Divider #(.width(32)) divider_2 (
    .a(divider_1_out), .b(32'ha), .out(divider_2_out), .rem({divider_2_rem, _3}));  // open: upper
  Divider #(.width(32)) divider_3 (
    .a(divider_2_out), .b(32'ha), .out(divider_3_out), .rem({divider_3_rem, _4}));  // open: upper
  Divider #(.width(32)) divider_4 (
    .a(divider_3_out), .b(32'ha), .out(divider_4_out), .rem({divider_4_rem, _5}));  // open: upper
  Divider #(.width(32)) divider_5 (
    .a(divider_4_out), .b(32'ha), .out(divider_5_out), .rem({divider_5_rem, _6}));  // open: upper
  Divider #(.width(32)) divider_6 (
    .a(divider_5_out), .b(32'ha), .out(divider_6_out), .rem({divider_6_rem, _7}));  // open: upper
  Divider #(.width(32)) divider_7 (
    .a(divider_6_out), .b(32'ha), .out(divider_7_out), .rem({divider_7_rem, _8}));  // open: upper
  Divider #(.width(32)) divider_8 (.a(divider_7_out), .b(32'ha), .rem({divider_8_rem, _9}));  // open: out, upper
  Divider #(.width(32)) divider_9 (.a(in_1), .b(32'ha), .out(divider_9_out), .rem({divider_9_rem, _0}));  // open: upper
  Divider #(.width(32)) divider_10 (
    .a(divider_9_out), .b(32'ha), .out(divider_10_out), .rem({divider_10_rem, _1}));  // open: upper
endmodule

module Display_12___4 (
  input  [11:0] in_1,
  output [3:0] _0,
  output [3:0] _1,
  output [3:0] _2,
  output [3:0] _3
);

  wire [11:0] divider_1_out, divider_3_out, divider_4_out;
  wire [11:4] divider_1_rem, divider_2_rem, divider_3_rem, divider_4_rem;

  Divider #(.width(12)) divider_1 (
    .a(divider_4_out), .b(12'ha), .out(divider_1_out), .rem({divider_1_rem, _2}));  // open: upper
  Divider #(.width(12)) divider_2 (.a(divider_1_out), .b(12'ha), .rem({divider_2_rem, _3}));  // open: out, upper
  Divider #(.width(12)) divider_3 (.a(in_1), .b(12'ha), .out(divider_3_out), .rem({divider_3_rem, _0}));  // open: upper
  Divider #(.width(12)) divider_4 (
    .a(divider_3_out), .b(12'ha), .out(divider_4_out), .rem({divider_4_rem, _1}));  // open: upper
endmodule

module Display_5___2 (
  input  [4:0] in_1,
  output [3:0] _0,
  output [3:0] _1
);

  wire [4:0] divider_1_out;
  wire [4:4] divider_1_rem, divider_2_rem;

  Divider #(.width(5)) divider_1 (
    .a(in_1), .b(5'b01010), .out(divider_1_out), .rem({divider_1_rem[4], _0}));  // open: upper
  Divider #(.width(5)) divider_2 (.a(divider_1_out), .b(5'b01010), .rem({divider_2_rem[4], _1}));  // open: out, upper
endmodule
