// Logisim project PC.circ as structural Verilog
module PC (
  input  [4:0] Op_Code,
  input  [9:0] Passo,
  input  Clock,
  input  Clear,
  input  [11:0] IMM,
  input  Zero,
  output [9:0] \Endereço 
);

  wire and_1_out, and_2_out, and_3_out, and_4_out, and_5_out, or_1_out;
  wire [9:0] adder_1_out, multiplexer_1_out, multiplexer_2_out;

  and and_1 (and_1_out, ~Op_Code[0], Op_Code[1], Op_Code[2], Op_Code[3], ~Op_Code[4]);  // AND_Gate
  and and_2 (and_2_out, Op_Code[0], Op_Code[1], Op_Code[2], Op_Code[3], ~Op_Code[4]);  // AND_Gate
  and and_3 (and_3_out, Op_Code[0], ~Op_Code[1], Op_Code[2], Op_Code[3], ~Op_Code[4]);  // AND_Gate
  and and_4 (and_4_out, Zero, and_1_out);
  and and_5 (and_5_out, ~Zero, and_2_out);  // AND_Gate
  or or_1 (or_1_out, and_4_out, and_5_out);
  Multiplexer #(.width(10), .enable("false")) multiplexer_1 (
    .in0(Passo), .in1(IMM[9:0]), .out(multiplexer_1_out), .sel(or_1_out));
  Multiplexer #(.width(10), .enable("false")) multiplexer_2 (
    .in0(adder_1_out), .in1(IMM[9:0]), .out(multiplexer_2_out), .sel(and_3_out));
  Register #(.width(10)) register_1 (.D(multiplexer_2_out), .Q(\Endereço ), .clk(Clock), .clr(Clear));  // open: en
  Adder #(.width(10)) adder_1 (.a(\Endereço ), .b(multiplexer_1_out), .out(adder_1_out), .cin(1'b0));  // open: cout

  // Notes on the sheet:
  //   BEQ
  //   BNQ
  //   Operações Base
  //   01101 JUMP
  //   01110 BEQ
  //   01111 BNQ
endmodule
