// Logisim project Projeto.circ as structural Verilog: 7 circuits, main circuit Apresentação
module \Apresentação  (
  input  in_1,
  output [31:0] out_2,
  output [31:0] out_3,
  output [4:0] out_4,
  output [31:0] out_5,
  output out_6,
  output out_7,
  output [11:0] out_8,
  output [4:0] out_9,
  output [4:0] out_10,
  output [4:0] out_11
);

  wire and_1_out, clock_1_out, not_1_out;
  wire [3:0] display_12_4_1__0, display_12_4_1__1, display_12_4_1__2, display_12_4_1__3, Op_Code__0,
       Op_Code__1, R_p1, R_p2, R_p3, R_p4, R_p5, R_p7, R_p8, R_p9, R_p10, R_p11, Rx__0, Rx__1, Rx__2, Rx__3,
       Rx__4, Rx__5, Rx__6, Rx__7, Rx__8, Rx__9, Ry__0, Ry__1, Ry__2, Ry__3, Ry__4, Ry__5, Ry__6, Ry__7,
       Ry__8, Ry__9, Sel_Rx__0, Sel_Rx__1, Sel_Ry__0, Sel_Ry__1, Sel_Write__0, Sel_Write__1;
  wire [9:0] \microprocessador_1_endereço , \microprocessador_1_load_store_endereço ;
  wire [31:0] microprocessador_1_store_data, ram_1_data, ram_2_data;

  Hex_Digit_Display hex_digit_display_1 (.value(Rx__9));  // open: dp
  Hex_Digit_Display hex_digit_display_2 (.value(Rx__7));  // open: dp
  Hex_Digit_Display hex_digit_display_3 (.value(Rx__8));  // open: dp
  Hex_Digit_Display hex_digit_display_4 (.value(Rx__6));  // open: dp
  Hex_Digit_Display hex_digit_display_5 (.value(Rx__5));  // open: dp
  RAM #(.addrWidth(10), .dataWidth(32)) ram_1 (
    .addr(\microprocessador_1_endereço ), .data(ram_1_data));  // open: sel, clk, ld, clr
  RAM #(.addrWidth(10), .dataWidth(32)) ram_2 (
    .addr(\microprocessador_1_load_store_endereço ), .data(ram_2_data), .clk(clock_1_out), .ld(not_1_out));  // open: sel, clr
  Hex_Digit_Display hex_digit_display_6 (.value(Rx__4));  // open: dp
  Hex_Digit_Display hex_digit_display_7 (.value(Rx__3));  // open: dp
  Display_32___9 Rx (
    .in_1(out_3), ._0(Rx__0), ._1(Rx__1), ._2(Rx__2), ._3(Rx__3), ._4(Rx__4), ._5(Rx__5), ._6(Rx__6),
    ._7(Rx__7), ._8(Rx__8), ._9(Rx__9));
  not not_1 (not_1_out, and_1_out);
  Hex_Digit_Display hex_digit_display_8 (.value(Rx__1));  // open: dp
  Hex_Digit_Display hex_digit_display_9 (.value(Rx__2));  // open: dp
  assign ram_2_data = and_1_out ? microprocessador_1_store_data : 32'bz;  // Controlled_Buffer controlled_buffer_1
  Clock clock_1 (.out(clock_1_out));
  Hex_Digit_Display hex_digit_display_10 (.value(Sel_Write__1));  // open: dp
  Hex_Digit_Display hex_digit_display_11 (.value(Sel_Write__0));  // open: dp
  Display_5___2 Sel_Write (.in_1(out_9), ._0(Sel_Write__0), ._1(Sel_Write__1));
  Hex_Digit_Display hex_digit_display_12 (.value(Rx__0));  // open: dp
  and and_1 (and_1_out, out_4[0], out_4[1], out_4[2], out_4[3], out_4[4]);
  Hex_Digit_Display hex_digit_display_13 (.value(Sel_Rx__1));  // open: dp
  Hex_Digit_Display hex_digit_display_14 (.value(Sel_Rx__0));  // open: dp
  Display_5___2 Sel_Rx (.in_1(out_10), ._0(Sel_Rx__0), ._1(Sel_Rx__1));
  Hex_Digit_Display hex_digit_display_15 (.value(Op_Code__1));  // open: dp
  MicroProcessador microprocessador_1 (
    .\Endereço (\microprocessador_1_endereço ), .Palavra(ram_1_data), .Write(clock_1_out), .Clear(in_1),
    .Sel_Write(out_9), .Sel_Rx(out_10), .R(out_5), .Overflow(out_6), .Zero(out_7), .Sel_Ry(out_11),
    .Rx(out_3), .Ry(out_2), .IMM(out_8), .Op_Code(out_4),
    .\Load_Store_Endereço (\microprocessador_1_load_store_endereço ), .Load_Data(ram_2_data),
    .Store_Data(microprocessador_1_store_data));
  Hex_Digit_Display hex_digit_display_16 (.value(Sel_Ry__1));  // open: dp
  Display_5___2 Sel_Ry (.in_1(out_11), ._0(Sel_Ry__0), ._1(Sel_Ry__1));
  Hex_Digit_Display hex_digit_display_17 (.value(Ry__9));  // open: dp
  Hex_Digit_Display hex_digit_display_18 (.value(Op_Code__0));  // open: dp
  Display_5___2 Op_Code (.in_1(out_4), ._0(Op_Code__0), ._1(Op_Code__1));
  Hex_Digit_Display hex_digit_display_19 (.value(Sel_Ry__0));  // open: dp
  Hex_Digit_Display hex_digit_display_20 (.value(Ry__7));  // open: dp
  Hex_Digit_Display hex_digit_display_21 (.value(Ry__8));  // open: dp
  Hex_Digit_Display hex_digit_display_22 (.value(R_p1));  // open: dp
  Hex_Digit_Display hex_digit_display_23 (.value(R_p2));  // open: dp
  Hex_Digit_Display hex_digit_display_24 (.value(display_12_4_1__2));  // open: dp
  Hex_Digit_Display hex_digit_display_25 (.value(display_12_4_1__3));  // open: dp
  Hex_Digit_Display hex_digit_display_26 (.value(Ry__5));  // open: dp
  Hex_Digit_Display hex_digit_display_27 (.value(Ry__6));  // open: dp
  Hex_Digit_Display hex_digit_display_28 (.value(R_p3));  // open: dp
  Hex_Digit_Display hex_digit_display_29 (.value(R_p4));  // open: dp
  Hex_Digit_Display hex_digit_display_30 (.value(display_12_4_1__1));  // open: dp
  Hex_Digit_Display hex_digit_display_31 (.value(display_12_4_1__0));  // open: dp
  Display_12___4 display_12_4_1 (
    .in_1(out_8), ._0(display_12_4_1__0), ._1(display_12_4_1__1), ._2(display_12_4_1__2),
    ._3(display_12_4_1__3));
  Hex_Digit_Display hex_digit_display_32 (.value(Ry__3));  // open: dp
  Hex_Digit_Display hex_digit_display_33 (.value(Ry__4));  // open: dp
  Display_32___9 Ry (
    .in_1(out_2), ._0(Ry__0), ._1(Ry__1), ._2(Ry__2), ._3(Ry__3), ._4(Ry__4), ._5(Ry__5), ._6(Ry__6),
    ._7(Ry__7), ._8(Ry__8), ._9(Ry__9));
  Hex_Digit_Display hex_digit_display_34 (.value(R_p7));  // open: dp
  Hex_Digit_Display hex_digit_display_35 (.value(R_p5));  // open: dp
  // Display_32___9 R: pin names not known; wires that end beside it: R_p1, R_p2, R_p3, R_p4, R_p5, out_5, R_p7, R_p8, R_p9, R_p10, R_p11
  Hex_Digit_Display hex_digit_display_36 (.value(Ry__1));  // open: dp
  Hex_Digit_Display hex_digit_display_37 (.value(Ry__2));  // open: dp
  Hex_Digit_Display hex_digit_display_38 (.value(R_p8));  // open: dp
  Hex_Digit_Display hex_digit_display_39 (.value(R_p9));  // open: dp
  Hex_Digit_Display hex_digit_display_40 (.value(Ry__0));  // open: dp
  Hex_Digit_Display hex_digit_display_41 (.value(R_p11));  // open: dp
  Hex_Digit_Display hex_digit_display_42 (.value(R_p10));  // open: dp
endmodule

module MicroProcessador (
  input  [31:0] Palavra,
  input  [31:0] Load_Data,
  input  Write,
  input  Clear,
  output [31:0] Rx,
  output [31:0] Ry,
  output [4:0] Sel_Rx,
  output [31:0] R,
  output [4:0] Sel_Write,
  output Overflow,
  output Zero,
  output [31:0] Store_Data,
  output [4:0] Sel_Ry,
  output [11:0] IMM,
  output [4:0] Op_Code,
  output [9:0] \Load_Store_Endereço ,
  output [9:0] \Endereço 
);

  wire io_dp_1_io___dp, not_1_out;
  wire [31:0] banco_de_registradores_1_ry, \entrada_br_1_saída , extensor_de_sinal_1_out_2;

  Leitor_da_Palavra leitor_da_palavra_1 (
    .Entrada(Palavra), .IMM(IMM), .Sel_Ry(Sel_Ry), .Sel_Rx(Sel_Rx), .Sel_Write(Sel_Write), .Op_Code(Op_Code));
  Entrada_BR entrada_br_1 (.OpCode(Op_Code), .ULA_S(R), .Load_Dado(Load_Data), .\Saída (\entrada_br_1_saída ));
  not not_1 (not_1_out, Write);
  Banco_de_Registradores banco_de_registradores_1 (
    .DataIn(\entrada_br_1_saída ), .Write(Write), .Rx(Rx), .Ry(banco_de_registradores_1_ry),
    .Sel_Write(Sel_Write), .Sel_Rx(Sel_Rx), .Sel_Ry(Sel_Ry), .Rw(Store_Data));
  Extensor_de_Sinal extensor_de_sinal_1 (.in_1(IMM), .out_2(extensor_de_sinal_1_out_2));
  PC pc_1 (
    .Clock(not_1_out), .Clear(Clear), .Passo(10'h1), .\Endereço (\Endereço ), .Op_Code(Op_Code), .IMM(IMM),
    .Zero(Zero));
  Multiplexer #(.width(32), .enable("false")) multiplexer_1 (
    .in0(banco_de_registradores_1_ry), .in1(extensor_de_sinal_1_out_2), .out(Ry), .sel(io_dp_1_io___dp));
  IO_DP io_dp_1 (.Op_Sel(Op_Code), .IO___DP(io_dp_1_io___dp));
  Conjunto conjunto_1 (.A(Rx), .B(Ry), .S(R), .Sel(Op_Code), .Zero(Zero), .Overflow(Overflow));
  Extensor_de_Sinal_32_10 extensor_de_sinal_32_10_1 (.out_2(\Load_Store_Endereço ), .in_1(R));

  // Notes on the sheet:
  //   Operações Base
  //   00000 AND 
  //   00001 OR
  //   00010 NAND
  //   00011 XOR
  //   00100 Somador Inteiros
  //   00101 Somador Naturais
  //   00110 Subtrator
  //   00111 Deslocamento Esquerda
  //   01000 Deslocamento Direita
  //   01001 Deslocamento Direita com Sinal
  //   01010 Rotação Esquerda
  //   01011 Rotação Direita
  //   01100 Menor que
  //   01101 JUMP
  //   01110 BEQ
  //   01111 BNQ
  //   Operações Novas
  //   11110  Load
  //   11111  Store
  //   Operações I
  //   10000 AND
  //   10001 OR
  //   10010 NAND
  //   10011 XOR
  //   10100 Somador Inteiros
  //   10101 Somador Naturais
  //   10110 Subtrator
  //   10111 Deslocamento Esquerda
  //   11000 Deslocamento Direita
  //   11001 Deslocamento Direita com Sinal
  //   11010 Rotação Esquerda
  //   11011 Rotação Direita
  //   11100  Menor que
endmodule

module IO_DP (
  input  [4:0] Op_Sel,
  output IO___DP
);


  assign IO___DP = Op_Sel[4];
  assign Op_Sel[2:0] = {3{Op_Sel[3]}};
  // also tied to GND on the sheet: Op_Sel[3]
endmodule

module Extensor_de_Sinal (
  input  [11:0] in_1,
  output [31:0] out_2
);


  assign out_2 = {{21{in_1[11]}}, in_1[10:0]};
endmodule

module Leitor_da_Palavra (
  input  [31:0] Entrada,
  output [11:0] IMM,
  output [4:0] Sel_Ry,
  output [4:0] Sel_Rx,
  output [4:0] Sel_Write,
  output [4:0] Op_Code
);


  assign IMM = Entrada[11:0];
  assign Op_Code = Entrada[31:27];
  assign Sel_Rx = Entrada[21:17];
  assign Sel_Ry = Entrada[16:12];
  assign Sel_Write = Entrada[26:22];
endmodule

module Extensor_de_Sinal_32_10 (
  input  [31:0] in_1,
  output [9:0] out_2
);


  assign in_1[30:10] = {21{in_1[31]}};
  assign out_2 = in_1[9:0];
endmodule

module Entrada_BR (
  input  [4:0] OpCode,
  input  [31:0] ULA_S,
  input  [31:0] Load_Dado,
  output [31:0] \Saída 
);

  wire and_1_out;

  and and_1 (and_1_out, ~OpCode[0], OpCode[1], OpCode[2], OpCode[3], OpCode[4]);  // AND_Gate
  Multiplexer #(.width(32), .enable("false")) multiplexer_1 (
    .in0(ULA_S), .in1(Load_Dado), .out(\Saída ), .sel(and_1_out));
endmodule
