// Logisim project Relógio.circ as structural Verilog: 8 circuits, main circuit Relógio
module \Relógio  (
  output Zerar
);

  wire binario_para_display_1_a, binario_para_display_1_b, binario_para_display_1_c,
       binario_para_display_1_d, binario_para_display_1_e, binario_para_display_1_f,
       binario_para_display_1_g, binario_para_display_2_a, binario_para_display_2_b,
       binario_para_display_2_c, binario_para_display_2_d, binario_para_display_2_e,
       binario_para_display_2_f, binario_para_display_2_g, binario_para_display_3_a,
       binario_para_display_3_b, binario_para_display_3_c, binario_para_display_3_d,
       binario_para_display_3_e, binario_para_display_3_f, binario_para_display_3_g,
       binario_para_display_4_a, binario_para_display_4_b, binario_para_display_4_c,
       binario_para_display_4_d, binario_para_display_4_e, binario_para_display_4_f,
       binario_para_display_4_g, binario_para_display_5_a, binario_para_display_5_b,
       binario_para_display_5_c, binario_para_display_5_d, binario_para_display_5_e,
       binario_para_display_5_f, binario_para_display_5_g, binario_para_display_6_a,
       binario_para_display_6_b, binario_para_display_6_c, binario_para_display_6_d,
       binario_para_display_6_e, binario_para_display_6_f, binario_para_display_6_g, clock_1_out,
       contador_0_5_com_soma_1_overflow, contador_0_5_com_soma_2_overflow, contador_0_9_1_overflow,
       contador_0_9_com_soma_1_overflow, contador_unidade_da_hora_1_overflow;
  wire [3:0] \contador_0_2_1_saída , \contador_0_5_com_soma_1_saída , \contador_0_5_com_soma_2_saída ,
       \contador_0_9_1_saída , \contador_0_9_com_soma_1_saída , \contador_unidade_da_hora_1_saída ,
       \flipflop_de4_bits_1_saída , \flipflop_de4_bits_2_saída , \flipflop_de4_bits_3_saída ,
       \flipflop_de4_bits_4_saída , \flipflop_de4_bits_5_saída , \flipflop_de4_bits_6_saída ;

  Clock clock_1 (.out(clock_1_out));
  Flipflop_de4_bits flipflop_de4_bits_1 (
    .Clock(clock_1_out), .Entrada(\contador_0_2_1_saída ), .\Saída (\flipflop_de4_bits_1_saída ));
  Contador_0_2 contador_0_2_1 (
    .Entrada(\flipflop_de4_bits_1_saída ), .Soma(contador_unidade_da_hora_1_overflow), .Overflow(Zerar),
    .\Saída (\contador_0_2_1_saída ));
  _7_Segment_Display u_7_segment_display_1 (
    .g(binario_para_display_1_a), .f(binario_para_display_1_b), .a(binario_para_display_1_c),
    .b(binario_para_display_1_d), .e(binario_para_display_1_e), .d(binario_para_display_1_f),
    .c(binario_para_display_1_g));  // open: dp
  Binario_para_Display binario_para_display_1 (
    .in_1(\contador_0_2_1_saída ), .a(binario_para_display_1_a), .b(binario_para_display_1_b),
    .c(binario_para_display_1_c), .d(binario_para_display_1_d), .e(binario_para_display_1_e),
    .f(binario_para_display_1_f), .g(binario_para_display_1_g));
  Flipflop_de4_bits flipflop_de4_bits_2 (
    .Clock(clock_1_out), .Entrada(\contador_unidade_da_hora_1_saída ), .\Saída (\flipflop_de4_bits_2_saída ));
  Contador_Unidade_da_Hora contador_unidade_da_hora_1 (
    .Dezena_da_Hora(\flipflop_de4_bits_1_saída ), .Entrada(\flipflop_de4_bits_2_saída ),
    .Soma(contador_0_5_com_soma_1_overflow), .Overflow(contador_unidade_da_hora_1_overflow),
    .\Saída (\contador_unidade_da_hora_1_saída ));
  _7_Segment_Display u_7_segment_display_2 (
    .g(binario_para_display_2_a), .f(binario_para_display_2_b), .a(binario_para_display_2_c),
    .b(binario_para_display_2_d), .e(binario_para_display_2_e), .d(binario_para_display_2_f),
    .c(binario_para_display_2_g));  // open: dp
  Binario_para_Display binario_para_display_2 (
    .in_1(\contador_unidade_da_hora_1_saída ), .a(binario_para_display_2_a), .b(binario_para_display_2_b),
    .c(binario_para_display_2_c), .d(binario_para_display_2_d), .e(binario_para_display_2_e),
    .f(binario_para_display_2_f), .g(binario_para_display_2_g));
  Flipflop_de4_bits flipflop_de4_bits_3 (
    .Clock(clock_1_out), .Entrada(\contador_0_5_com_soma_1_saída ), .\Saída (\flipflop_de4_bits_3_saída ));
  Contador_0_5_com_Soma contador_0_5_com_soma_1 (
    .Entrada(\flipflop_de4_bits_3_saída ), .Soma(contador_0_9_com_soma_1_overflow),
    .Overflow(contador_0_5_com_soma_1_overflow), .\Saída (\contador_0_5_com_soma_1_saída ));
  _7_Segment_Display u_7_segment_display_3 (
    .g(binario_para_display_3_a), .f(binario_para_display_3_b), .a(binario_para_display_3_c),
    .b(binario_para_display_3_d), .e(binario_para_display_3_e), .d(binario_para_display_3_f),
    .c(binario_para_display_3_g));  // open: dp
  Binario_para_Display binario_para_display_3 (
    .in_1(\contador_0_5_com_soma_1_saída ), .a(binario_para_display_3_a), .b(binario_para_display_3_b),
    .c(binario_para_display_3_c), .d(binario_para_display_3_d), .e(binario_para_display_3_e),
    .f(binario_para_display_3_f), .g(binario_para_display_3_g));
  Flipflop_de4_bits flipflop_de4_bits_4 (
    .Clock(clock_1_out), .Entrada(\contador_0_9_com_soma_1_saída ), .\Saída (\flipflop_de4_bits_4_saída ));
  Binario_para_Display binario_para_display_4 (
    .in_1(\contador_0_9_com_soma_1_saída ), .a(binario_para_display_4_a), .b(binario_para_display_4_b),
    .c(binario_para_display_4_c), .d(binario_para_display_4_d), .e(binario_para_display_4_e),
    .f(binario_para_display_4_f), .g(binario_para_display_4_g));
  Contador_0_9_com_Soma contador_0_9_com_soma_1 (
    .Entrada(\flipflop_de4_bits_4_saída ), .Soma(contador_0_5_com_soma_2_overflow),
    .Overflow(contador_0_9_com_soma_1_overflow), .\Saída (\contador_0_9_com_soma_1_saída ));
  _7_Segment_Display u_7_segment_display_4 (
    .g(binario_para_display_4_a), .f(binario_para_display_4_b), .a(binario_para_display_4_c),
    .b(binario_para_display_4_d), .e(binario_para_display_4_e), .d(binario_para_display_4_f),
    .c(binario_para_display_4_g));  // open: dp
  Flipflop_de4_bits flipflop_de4_bits_5 (
    .Clock(clock_1_out), .Entrada(\contador_0_5_com_soma_2_saída ), .\Saída (\flipflop_de4_bits_5_saída ));
  _7_Segment_Display u_7_segment_display_5 (
    .g(binario_para_display_5_a), .f(binario_para_display_5_b), .a(binario_para_display_5_c),
    .b(binario_para_display_5_d), .e(binario_para_display_5_e), .d(binario_para_display_5_f),
    .c(binario_para_display_5_g));  // open: dp
  Binario_para_Display binario_para_display_5 (
    .in_1(\contador_0_5_com_soma_2_saída ), .a(binario_para_display_5_a), .b(binario_para_display_5_b),
    .c(binario_para_display_5_c), .d(binario_para_display_5_d), .e(binario_para_display_5_e),
    .f(binario_para_display_5_f), .g(binario_para_display_5_g));
  Contador_0_5_com_Soma contador_0_5_com_soma_2 (
    .Entrada(\flipflop_de4_bits_5_saída ), .Soma(contador_0_9_1_overflow),
    .Overflow(contador_0_5_com_soma_2_overflow), .\Saída (\contador_0_5_com_soma_2_saída ));
  Flipflop_de4_bits flipflop_de4_bits_6 (
    .Clock(clock_1_out), .Entrada(\contador_0_9_1_saída ), .\Saída (\flipflop_de4_bits_6_saída ));
  _7_Segment_Display u_7_segment_display_6 (
    .g(binario_para_display_6_a), .f(binario_para_display_6_b), .a(binario_para_display_6_c),
    .b(binario_para_display_6_d), .e(binario_para_display_6_e), .d(binario_para_display_6_f),
    .c(binario_para_display_6_g));  // open: dp
  Binario_para_Display binario_para_display_6 (
    .in_1(\contador_0_9_1_saída ), .a(binario_para_display_6_a), .b(binario_para_display_6_b),
    .c(binario_para_display_6_c), .d(binario_para_display_6_d), .e(binario_para_display_6_e),
    .f(binario_para_display_6_f), .g(binario_para_display_6_g));
  Contador_0_9 contador_0_9_1 (
    .Entrada(\flipflop_de4_bits_6_saída ), .Overflow(contador_0_9_1_overflow),
    .\Saída (\contador_0_9_1_saída ));
endmodule

module Binario_para_Display (
  input  [3:0] in_1,
  output a,
  output b,
  output c,
  output d,
  output e,
  output f,
  output g
);

  wire and_1_out, and_2_out, or_1_out, or_2_out, or_3_out, or_4_out, or_5_out, or_6_out, or_7_out, or_8_out,
       or_9_out, or_10_out, or_11_out, or_12_out;

  or or_1 (or_1_out, in_1[1], in_1[2], in_1[3]);
  or or_2 (or_2_out, ~in_1[0], ~in_1[1], ~in_1[2], in_1[3]);  // OR_Gate
  or or_3 (or_3_out, in_1[3], in_1[2], ~in_1[0]);  // OR_Gate
  or or_4 (or_4_out, in_1[3], ~in_1[1], ~in_1[0]);  // OR_Gate
  or or_5 (or_5_out, in_1[3], in_1[2], ~in_1[1]);  // OR_Gate
  or or_6 (or_6_out, in_1[3], in_1[2], in_1[1], ~in_1[0]);  // OR_Gate
  or or_7 (or_7_out, in_1[3], ~in_1[2], in_1[1], in_1[0]);  // OR_Gate
  or or_8 (or_8_out, in_1[3], ~in_1[2], in_1[1], ~in_1[0]);  // OR_Gate
  or or_9 (or_9_out, in_1[3], ~in_1[2], ~in_1[1], in_1[0]);  // OR_Gate
  and and_1 (and_1_out, ~in_1[2], ~in_1[1], ~in_1[0]);  // AND_Gate
  and and_2 (and_2_out, ~in_1[3], in_1[1], ~in_1[0]);  // AND_Gate
  or or_10 (or_10_out, in_1[3], in_1[2], in_1[1], ~in_1[0]);  // OR_Gate
  or or_11 (or_11_out, in_1[3], ~in_1[2], ~in_1[1], ~in_1[0]);  // OR_Gate
  or or_12 (or_12_out, in_1[3], ~in_1[2], in_1[1], in_1[0]);  // OR_Gate
  and and_3 (a, or_1_out, or_2_out);
  and and_4 (b, or_3_out, or_4_out, or_5_out);
  and and_5 (c, or_6_out, or_7_out);
  and and_6 (d, or_8_out, or_9_out);
  or or_13 (e, and_1_out, and_2_out);
  and and_7 (f, or_10_out, or_11_out, or_12_out);
  nand nand_1 (g, ~in_1[0], in_1[1], ~in_1[2], ~in_1[3]);  // NAND_Gate
endmodule

module Flipflop_de4_bits (
  input  Clock,
  input  [3:0] Entrada,
  output [3:0] \Saída 
);

  D_Flip_Flop d_ff_1 (.clk(Clock), .D(Entrada[0]), .Q(\Saída [0]));  // open: Qn, preset, en, reset
  D_Flip_Flop d_ff_2 (.clk(Clock), .D(Entrada[1]), .Q(\Saída [1]));  // open: Qn, preset, en, reset
  D_Flip_Flop d_ff_3 (.clk(Clock), .D(Entrada[2]), .Q(\Saída [2]));  // open: Qn, preset, en, reset
  D_Flip_Flop d_ff_4 (.clk(Clock), .D(Entrada[3]), .Q(\Saída [3]));  // open: Qn, preset, en, reset
endmodule

module Contador_0_9 (
  input  [3:0] Entrada,
  output Overflow,
  output [3:0] \Saída 
);

  wire [3:0] adder_1_out;

  Adder #(.width(4)) adder_1 (.a(Entrada), .b(4'b0001), .out(adder_1_out));  // open: cin, cout
  and and_1 (Overflow, Entrada[0], ~Entrada[1], ~Entrada[2], Entrada[3]);  // AND_Gate
  Multiplexer #(.width(4), .enable("false")) multiplexer_1 (
    .in0(adder_1_out), .in1(4'b0000), .out(\Saída ), .sel(Overflow));
endmodule

module Contador_0_5_com_Soma (
  input  [3:0] Entrada,
  input  Soma,
  output Overflow,
  output [3:0] \Saída 
);

  wire and_1_out;
  wire [3:0] adder_1_out, multiplexer_1_out;

  Adder #(.width(4)) adder_1 (.a(Entrada), .b(4'b0001), .out(adder_1_out));  // open: cin, cout
  Multiplexer #(.width(4), .enable("false")) multiplexer_1 (
    .in0(Entrada), .in1(adder_1_out), .out(multiplexer_1_out), .sel(Soma));
  and and_1 (and_1_out, Entrada[0], ~Entrada[1], Entrada[2], ~Entrada[3]);  // AND_Gate
  Multiplexer #(.width(4), .enable("false")) multiplexer_2 (
    .in0(multiplexer_1_out), .in1(4'b0000), .out(\Saída ), .sel(Overflow));
  and and_2 (Overflow, and_1_out, Soma);
endmodule

module Contador_0_9_com_Soma (
  input  [3:0] Entrada,
  input  Soma,
  output Overflow,
  output [3:0] \Saída 
);

  wire and_1_out;
  wire [3:0] adder_1_out, multiplexer_1_out;

  Adder #(.width(4)) adder_1 (.a(Entrada), .b(4'b0001), .out(adder_1_out));  // open: cin, cout
  Multiplexer #(.width(4), .enable("false")) multiplexer_1 (
    .in0(Entrada), .in1(adder_1_out), .out(multiplexer_1_out), .sel(Soma));
  and and_1 (and_1_out, Entrada[0], ~Entrada[1], ~Entrada[2], Entrada[3]);  // AND_Gate
  Multiplexer #(.width(4), .enable("false")) multiplexer_2 (
    .in0(multiplexer_1_out), .in1(4'b0000), .out(\Saída ), .sel(Overflow));
  and and_2 (Overflow, and_1_out, Soma);
endmodule

module Contador_Unidade_da_Hora (
  input  [3:0] Dezena_da_Hora,
  input  [3:0] Entrada,
  input  Soma,
  output Overflow,
  output [3:0] \Saída 
);

  wire and_1_out, and_2_out, and_3_out, multiplexer_2_out;
  wire [3:0] adder_1_out, multiplexer_1_out;

  and and_1 (and_1_out, ~Dezena_da_Hora[0], Dezena_da_Hora[1], ~Dezena_da_Hora[2], ~Dezena_da_Hora[3]);  // AND_Gate
  Adder #(.width(4)) adder_1 (.a(Entrada), .b(4'b0001), .out(adder_1_out));  // open: cin, cout
  and and_2 (and_2_out, Entrada[0], ~Entrada[1], ~Entrada[2], Entrada[3]);  // AND_Gate
  and and_3 (and_3_out, Entrada[0], Entrada[1], ~Entrada[2], ~Entrada[3]);  // AND_Gate
  Multiplexer #(.width(4), .enable("false")) multiplexer_1 (
    .in0(Entrada), .in1(adder_1_out), .out(multiplexer_1_out), .sel(Soma));
  Multiplexer #(.enable("false")) multiplexer_2 (
    .in0(and_2_out), .in1(and_3_out), .out(multiplexer_2_out), .sel(and_1_out));
  Multiplexer #(.width(4), .enable("false")) multiplexer_3 (
    .in0(multiplexer_1_out), .in1(4'b0000), .out(\Saída ), .sel(Overflow));
  and and_4 (Overflow, multiplexer_2_out, Soma);
endmodule

module Contador_0_2 (
  input  [3:0] Entrada,
  input  Soma,
  output Overflow,
  output [3:0] \Saída 
);

  wire and_1_out;
  wire [3:0] adder_1_out, multiplexer_1_out;

  Adder #(.width(4)) adder_1 (.a(Entrada), .b(4'b0001), .out(adder_1_out));  // open: cin, cout
  Multiplexer #(.width(4), .enable("false")) multiplexer_1 (
    .in0(Entrada), .in1(adder_1_out), .out(multiplexer_1_out), .sel(Soma));
  and and_1 (and_1_out, ~Entrada[0], Entrada[1], ~Entrada[2], ~Entrada[3]);  // AND_Gate
  Multiplexer #(.width(4), .enable("false")) multiplexer_2 (
    .in0(multiplexer_1_out), .in1(4'b0000), .out(\Saída ), .sel(Overflow));
  and and_2 (Overflow, and_1_out, Soma);
endmodule
