// Logisim project ULA.circ as structural Verilog: 7 circuits, main circuit Apresentação
module \Célula  (
  input  [4:0] sel,
  input  a,
  input  b,
  input  cIn,
  input  Left,
  output S,
  output cOut,
  output Right
);

  wire adder_1_cout, adder_1_out, and_1_out, and_2_out, and_3_out, and_4_out, nand_1_out, or_1_out, or_2_out,
       subtractor_1_bout, subtractor_1_out, xor_1_out;

  Subtractor #(.width(1)) subtractor_1 (.a(a), .b(b), .out(subtractor_1_out), .bin(cIn), .bout(subtractor_1_bout));
  and and_1 (and_1_out, a, b);
  or or_1 (or_1_out, a, b);
  nand nand_1 (nand_1_out, a, b);
  xor xor_1 (xor_1_out, a, b);
  Adder #(.width(1)) adder_1 (.a(a), .b(b), .out(adder_1_out), .cin(cIn), .cout(adder_1_cout));
  Multiplexer #(.select(5), .enable("false")) multiplexer_1 (
    .in0(and_1_out), .in1(or_1_out), .in2(nand_1_out), .in3(xor_1_out), .in4(adder_1_out), .in5(adder_1_out),
    .in6(subtractor_1_out), .in7(cIn), .in8(Left), .in9(Left), .in10(cIn), .in11(Left),
    .in12(subtractor_1_out), .in13(1'b0), .in14(subtractor_1_out), .in15(subtractor_1_out), .in16(and_1_out),
    .in17(or_1_out), .in18(nand_1_out), .in19(xor_1_out), .in20(adder_1_out), .in21(adder_1_out),
    .in22(subtractor_1_out), .in23(cIn), .in24(Left), .in25(Left), .in26(cIn), .in27(Left),
    .in28(subtractor_1_out), .in29(1'b0), .in30(adder_1_out), .in31(adder_1_out), .out(S), .sel(sel));
  Multiplexer #(.select(5), .enable("false")) multiplexer_2 (
    .in0(1'b0), .in1(1'b0), .in2(1'b0), .in3(1'b0), .in4(adder_1_cout), .in5(adder_1_cout),
    .in6(subtractor_1_bout), .in7(a), .in8(1'b0), .in9(1'b0), .in10(a), .in11(1'b0),
    .in12(subtractor_1_bout), .in13(1'b0), .in14(subtractor_1_bout), .in15(subtractor_1_bout), .in16(1'b0),
    .in17(1'b0), .in18(1'b0), .in19(1'b0), .in20(adder_1_cout), .in21(adder_1_cout),
    .in22(subtractor_1_bout), .in23(a), .in24(1'b0), .in25(1'b0), .in26(a), .in27(1'b0),
    .in28(subtractor_1_bout), .in29(1'b0), .in30(adder_1_cout), .in31(adder_1_cout), .out(cOut), .sel(sel));
  or or_2 (or_2_out, ~sel[4], sel[4]);  // OR_Gate
  and and_2 (and_2_out, a, or_2_out, sel[3], ~sel[2], ~sel[1], ~sel[0]);  // AND_Gate
  and and_3 (and_3_out, a, or_2_out, sel[3], ~sel[2], ~sel[1], sel[0]);  // AND_Gate
  or or_3 (Right, and_2_out, and_3_out, and_4_out);
  and and_4 (and_4_out, a, or_2_out, sel[3], ~sel[2], sel[1], sel[0]);  // AND_Gate

  // Notes on the sheet:
  //   Operações Base
  //   00000 AND 
  //   00001 OR
  //   00010 NAND
  //   00011 XOR
  //   00100 Somador Inteiros
  //   00101 Somador Naturais
  //   00110 Subtrator
  //   00111 Deslocamento Esquerda
  //   01000 Deslocamento Direita
  //   01001 Deslocamento Direita com Sinal
  //   01010 Rotação Esquerda
  //   01011 Rotação Direita
  //   01100 Menor que
  //   01101 JUMP
  //   01110 BEQ
  //   01111 BNQ
  //   Operações I
  //   10000 AND
  //   10001 OR
  //   10010 NAND
  //   10011 XOR
  //   10100 Somador Inteiros
  //   10101 Somador Naturais
  //   10110 Subtrator
  //   10111 Deslocamento Esquerda
  //   11000 Deslocamento Direita
  //   11001 Deslocamento Direita com Sinal
  //   11010 Rotação Esquerda
  //   11011 Rotação Direita
  //   11100  Menor que
  //   Operações Novas
  //   11110  Load
  //   11111  Store
endmodule

module Conjunto (
  input  [31:0] A,
  input  [4:0] Sel,
  input  [31:0] B,
  output Overflow,
  output Zero,
  output [31:0] S
);

  wire conjunto_esquerda_mais_significativa_1_left31, conjunto_menor_que_mux_1_mux,
       \conjunto_rotação_esquerda_1_cin0 , \célula_1_cout , \célula_1_right , \célula_2_cout ,
       \célula_2_right , \célula_3_cout , \célula_3_right , \célula_4_cout , \célula_4_right ,
       \célula_5_cout , \célula_5_right , \célula_6_cout , \célula_6_right , \célula_7_cout ,
       \célula_7_right , \célula_8_cout , \célula_8_right , \célula_9_cout , \célula_9_right ,
       \célula_10_cout , \célula_10_right , \célula_11_cout , \célula_11_right , \célula_12_cout ,
       \célula_12_right , \célula_13_cout , \célula_13_right , \célula_14_cout , \célula_14_right ,
       \célula_15_cout , \célula_15_right , \célula_16_cout , \célula_16_right , \célula_17_cout ,
       \célula_17_right , \célula_18_cout , \célula_18_right , \célula_19_cout , \célula_19_right ,
       \célula_20_cout , \célula_20_right , \célula_21_cout , \célula_21_right , \célula_22_cout ,
       \célula_22_right , \célula_23_cout , \célula_23_right , \célula_24_cout , \célula_24_right ,
       \célula_25_cout , \célula_25_right , \célula_26_cout , \célula_26_right , \célula_27_cout ,
       \célula_27_right , \célula_28_cout , \célula_28_right , \célula_29_cout , \célula_29_right ,
       \célula_30_cout , \célula_30_right , \célula_31_cout , \célula_31_right , \célula_32_cout ,
       \célula_32_right , overflow_1_overflow;
  wire [31:0] conjunto_menor_que_mux_1_s, \célula_32_s ;

  Conjunto___Esquerda_Mais_Significativa conjunto_esquerda_mais_significativa_1 (
    .a31(A[31]), .Sel_Op(Sel), .Right0(\célula_32_right ),
    .Left31(conjunto_esquerda_mais_significativa_1_left31));
  Overflow overflow_1 (.Sel(Sel), .a(A[31]), .b(B[31]), .cOut(\célula_32_s [31]), .overflow(overflow_1_overflow));
  \Célula  \célula_1  (
    .a(A[30]), .b(B[30]), .cIn(\célula_3_cout ), .Left(\célula_2_right ), .S(\célula_32_s [30]),
    .cOut(\célula_1_cout ), .sel(Sel), .Right(\célula_1_right ));
  \Célula  \célula_2  (
    .a(A[31]), .b(B[31]), .cIn(\célula_1_cout ), .Left(conjunto_esquerda_mais_significativa_1_left31),
    .S(\célula_32_s [31]), .cOut(\célula_2_cout ), .sel(Sel), .Right(\célula_2_right ));
  or or_1 (Overflow, overflow_1_overflow, \célula_2_cout );
  \Célula  \célula_3  (
    .a(A[29]), .b(B[29]), .cIn(\célula_5_cout ), .Left(\célula_1_right ), .S(\célula_32_s [29]),
    .cOut(\célula_3_cout ), .sel(Sel), .Right(\célula_3_right ));
  \Conjunto___Rotação_Esquerda  \conjunto_rotação_esquerda_1  (
    .a31(A[31]), .Sel_Op(Sel), .cIn0(\conjunto_rotação_esquerda_1_cin0 ));
  \Célula  \célula_4  (
    .a(A[27]), .b(B[27]), .cIn(\célula_7_cout ), .Left(\célula_5_right ), .S(\célula_32_s [27]),
    .cOut(\célula_4_cout ), .sel(Sel), .Right(\célula_4_right ));
  \Célula  \célula_5  (
    .a(A[28]), .b(B[28]), .cIn(\célula_4_cout ), .Left(\célula_3_right ), .S(\célula_32_s [28]),
    .cOut(\célula_5_cout ), .sel(Sel), .Right(\célula_5_right ));
  \Célula  \célula_6  (
    .a(A[25]), .b(B[25]), .cIn(\célula_8_cout ), .Left(\célula_7_right ), .S(\célula_32_s [25]),
    .cOut(\célula_6_cout ), .sel(Sel), .Right(\célula_6_right ));
  \Célula  \célula_7  (
    .a(A[26]), .b(B[26]), .cIn(\célula_6_cout ), .Left(\célula_4_right ), .S(\célula_32_s [26]),
    .cOut(\célula_7_cout ), .sel(Sel), .Right(\célula_7_right ));
  \Célula  \célula_8  (
    .a(A[24]), .b(B[24]), .cIn(\célula_10_cout ), .Left(\célula_6_right ), .S(\célula_32_s [24]),
    .cOut(\célula_8_cout ), .sel(Sel), .Right(\célula_8_right ));
  \Célula  \célula_9  (
    .a(A[22]), .b(B[22]), .cIn(\célula_11_cout ), .Left(\célula_10_right ), .S(\célula_32_s [22]),
    .cOut(\célula_9_cout ), .sel(Sel), .Right(\célula_9_right ));
  \Célula  \célula_10  (
    .a(A[23]), .b(B[23]), .cIn(\célula_9_cout ), .Left(\célula_8_right ), .S(\célula_32_s [23]),
    .cOut(\célula_10_cout ), .sel(Sel), .Right(\célula_10_right ));
  \Célula  \célula_11  (
    .a(A[21]), .b(B[21]), .cIn(\célula_13_cout ), .Left(\célula_9_right ), .S(\célula_32_s [21]),
    .cOut(\célula_11_cout ), .sel(Sel), .Right(\célula_11_right ));
  \Célula  \célula_12  (
    .a(A[19]), .b(B[19]), .cIn(\célula_15_cout ), .Left(\célula_13_right ), .S(\célula_32_s [19]),
    .cOut(\célula_12_cout ), .sel(Sel), .Right(\célula_12_right ));
  \Célula  \célula_13  (
    .a(A[20]), .b(B[20]), .cIn(\célula_12_cout ), .Left(\célula_11_right ), .S(\célula_32_s [20]),
    .cOut(\célula_13_cout ), .sel(Sel), .Right(\célula_13_right ));
  \Célula  \célula_14  (
    .a(A[17]), .b(B[17]), .cIn(\célula_16_cout ), .Left(\célula_15_right ), .S(\célula_32_s [17]),
    .cOut(\célula_14_cout ), .sel(Sel), .Right(\célula_14_right ));
  \Célula  \célula_15  (
    .a(A[18]), .b(B[18]), .cIn(\célula_14_cout ), .Left(\célula_12_right ), .S(\célula_32_s [18]),
    .cOut(\célula_15_cout ), .sel(Sel), .Right(\célula_15_right ));
  \Célula  \célula_16  (
    .a(A[16]), .b(B[16]), .cIn(\célula_18_cout ), .Left(\célula_14_right ), .S(\célula_32_s [16]),
    .cOut(\célula_16_cout ), .sel(Sel), .Right(\célula_16_right ));
  \Célula  \célula_17  (
    .a(A[14]), .b(B[14]), .cIn(\célula_19_cout ), .Left(\célula_18_right ), .S(\célula_32_s [14]),
    .cOut(\célula_17_cout ), .sel(Sel), .Right(\célula_17_right ));
  \Célula  \célula_18  (
    .a(A[15]), .b(B[15]), .cIn(\célula_17_cout ), .Left(\célula_16_right ), .S(\célula_32_s [15]),
    .cOut(\célula_18_cout ), .sel(Sel), .Right(\célula_18_right ));
  \Célula  \célula_19  (
    .a(A[13]), .b(B[13]), .cIn(\célula_21_cout ), .Left(\célula_17_right ), .S(\célula_32_s [13]),
    .cOut(\célula_19_cout ), .sel(Sel), .Right(\célula_19_right ));
  Conjunto___Menor_Que_MUX conjunto_menor_que_mux_1 (
    .a31(A[31]), .b31(B[31]), .Overflow(Overflow), .Sel_Op(Sel), .MUX(conjunto_menor_que_mux_1_mux),
    .S(conjunto_menor_que_mux_1_s));
  \Célula  \célula_20  (
    .a(A[11]), .b(B[11]), .cIn(\célula_23_cout ), .Left(\célula_21_right ), .S(\célula_32_s [11]),
    .cOut(\célula_20_cout ), .sel(Sel), .Right(\célula_20_right ));
  \Célula  \célula_21  (
    .a(A[12]), .b(B[12]), .cIn(\célula_20_cout ), .Left(\célula_19_right ), .S(\célula_32_s [12]),
    .cOut(\célula_21_cout ), .sel(Sel), .Right(\célula_21_right ));
  \Célula  \célula_22  (
    .a(A[9]), .b(B[9]), .cIn(\célula_24_cout ), .Left(\célula_23_right ), .S(\célula_32_s [9]),
    .cOut(\célula_22_cout ), .sel(Sel), .Right(\célula_22_right ));
  \Célula  \célula_23  (
    .a(A[10]), .b(B[10]), .cIn(\célula_22_cout ), .Left(\célula_20_right ), .S(\célula_32_s [10]),
    .cOut(\célula_23_cout ), .sel(Sel), .Right(\célula_23_right ));
  \Célula  \célula_24  (
    .a(A[8]), .b(B[8]), .cIn(\célula_26_cout ), .Left(\célula_22_right ), .S(\célula_32_s [8]),
    .cOut(\célula_24_cout ), .sel(Sel), .Right(\célula_24_right ));
  Multiplexer #(.width(32), .enable("false")) multiplexer_1 (
    .in0(\célula_32_s ), .in1(conjunto_menor_que_mux_1_s), .out(S), .sel(conjunto_menor_que_mux_1_mux));
  \Célula  \célula_25  (
    .a(A[6]), .b(B[6]), .cIn(\célula_27_cout ), .Left(\célula_26_right ), .S(\célula_32_s [6]),
    .cOut(\célula_25_cout ), .sel(Sel), .Right(\célula_25_right ));
  \Célula  \célula_26  (
    .a(A[7]), .b(B[7]), .cIn(\célula_25_cout ), .Left(\célula_24_right ), .S(\célula_32_s [7]),
    .cOut(\célula_26_cout ), .sel(Sel), .Right(\célula_26_right ));
  \Célula  \célula_27  (
    .a(A[5]), .b(B[5]), .cIn(\célula_29_cout ), .Left(\célula_25_right ), .S(\célula_32_s [5]),
    .cOut(\célula_27_cout ), .sel(Sel), .Right(\célula_27_right ));
  \Célula  \célula_28  (
    .a(A[3]), .b(B[3]), .cIn(\célula_31_cout ), .Left(\célula_29_right ), .S(\célula_32_s [3]),
    .cOut(\célula_28_cout ), .sel(Sel), .Right(\célula_28_right ));
  \Célula  \célula_29  (
    .a(A[4]), .b(B[4]), .cIn(\célula_28_cout ), .Left(\célula_27_right ), .S(\célula_32_s [4]),
    .cOut(\célula_29_cout ), .sel(Sel), .Right(\célula_29_right ));
  \Célula  \célula_30  (
    .a(A[1]), .b(B[1]), .cIn(\célula_32_cout ), .Left(\célula_31_right ), .S(\célula_32_s [1]),
    .cOut(\célula_30_cout ), .sel(Sel), .Right(\célula_30_right ));
  \Célula  \célula_31  (
    .a(A[2]), .b(B[2]), .cIn(\célula_30_cout ), .Left(\célula_28_right ), .S(\célula_32_s [2]),
    .cOut(\célula_31_cout ), .sel(Sel), .Right(\célula_31_right ));
  and and_1 (Zero, ~\célula_32_s [31], ~\célula_32_s [30], ~\célula_32_s [29], ~\célula_32_s [28], ~\célula_32_s [27], ~\célula_32_s [26], ~\célula_32_s [25], ~\célula_32_s [24], ~\célula_32_s [23], ~\célula_32_s [22], ~\célula_32_s [21], ~\célula_32_s [20], ~\célula_32_s [19], ~\célula_32_s [18], ~\célula_32_s [17], ~\célula_32_s [16], ~\célula_32_s [15], ~\célula_32_s [14], ~\célula_32_s [13], ~\célula_32_s [12], ~\célula_32_s [11], ~\célula_32_s [10], ~\célula_32_s [9], ~\célula_32_s [8], ~\célula_32_s [7], ~\célula_32_s [6], ~\célula_32_s [5], ~\célula_32_s [4], ~\célula_32_s [3], ~\célula_32_s [2], ~\célula_32_s [1], ~\célula_32_s [0]);  // AND_Gate
  \Célula  \célula_32  (
    .a(A[0]), .b(B[0]), .cIn(\conjunto_rotação_esquerda_1_cin0 ), .Left(\célula_30_right ),
    .S(\célula_32_s [0]), .cOut(\célula_32_cout ), .sel(Sel), .Right(\célula_32_right ));
endmodule

module Conjunto___Esquerda_Mais_Significativa (
  input  a31,
  input  [4:0] Sel_Op,
  input  Right0,
  output Left31
);

  wire and_1_out, and_2_out, and_3_out, and_4_out, or_1_out, or_2_out;

  or or_1 (or_1_out, Sel_Op[4], ~Sel_Op[4]);  // OR_Gate
  or or_2 (or_2_out, Sel_Op[4], ~Sel_Op[4]);  // OR_Gate
  and and_1 (and_1_out, Sel_Op[0], ~Sel_Op[1], ~Sel_Op[2], Sel_Op[3], or_2_out);  // AND_Gate
  and and_2 (and_2_out, Sel_Op[0], Sel_Op[1], ~Sel_Op[2], Sel_Op[3], or_1_out);  // AND_Gate
  and and_3 (and_3_out, a31, and_1_out);
  and and_4 (and_4_out, and_2_out, Right0);
  or or_3 (Left31, and_3_out, and_4_out);

  // Notes on the sheet:
  //   Operações Base
  //   01001 Deslocamento Direita com Sinal
  //   01011 Rotação Direita
  //   Operações I
  //   11001 Deslocamento Direita com Sinal
  //   11011 Rotação Direita
endmodule

module \Conjunto___Rotação_Esquerda  (
  input  a31,
  input  [4:0] Sel_Op,
  output cIn0
);

  wire and_1_out, or_1_out;

  or or_1 (or_1_out, Sel_Op[4], ~Sel_Op[4]);  // OR_Gate
  and and_1 (and_1_out, ~Sel_Op[0], Sel_Op[1], ~Sel_Op[2], Sel_Op[3], or_1_out);  // AND_Gate
  and and_2 (cIn0, a31, and_1_out);

  // Notes on the sheet:
  //   Operações Base
  //   01010 Rotação Esquerda
  //   Operações I
  //   11010 Rotação Esquerda
endmodule

module Conjunto___Menor_Que_MUX (
  input  a31,
  input  b31,
  input  Overflow,
  input  [4:0] Sel_Op,
  output MUX,
  output [31:0] S
);

  wire and_2_out, and_3_out, and_4_out, or_1_out;

  or or_1 (or_1_out, Sel_Op[4], ~Sel_Op[4]);  // OR_Gate
  and and_1 (MUX, ~Sel_Op[0], ~Sel_Op[1], Sel_Op[2], Sel_Op[3], or_1_out);  // AND_Gate
  and and_2 (and_2_out, MUX, Overflow, ~and_4_out);  // AND_Gate
  and and_3 (and_3_out, MUX, ~Overflow, and_4_out);  // AND_Gate
  or or_2 (S[0], and_2_out, and_3_out);
  and and_4 (and_4_out, b31, ~a31);  // AND_Gate

  assign S[31:1] = {31{1'b0}};

  // Notes on the sheet:
  //   Operações Base
  //   01100 Menor que
  //   Operações I
  //   11100  Menor que
endmodule

module Overflow (
  input  [4:0] Sel,
  input  a,
  input  b,
  input  cOut,
  output overflow
);

  wire and_1_out, and_2_out, and_3_out, or_1_out;

  and and_1 (and_1_out, ~Sel[0], ~Sel[1], Sel[2], ~Sel[3], ~Sel[4]);  // AND_Gate
  and and_2 (and_2_out, ~a, ~b, cOut);  // AND_Gate
  and and_3 (and_3_out, a, b, ~cOut);  // AND_Gate
  or or_1 (or_1_out, and_2_out, and_3_out);
  and and_4 (overflow, and_1_out, or_1_out);
endmodule

module \Apresentação  (
  input  [31:0] a,
  input  [31:0] b,
  input  [4:0] Sel,
  output [31:0] S,
  output Overflow,
  output Zero
);

  Conjunto conjunto_1 (.A(a), .B(b), .S(S), .Sel(Sel), .Zero(Zero), .Overflow(Overflow));

  // Notes on the sheet:
  //   Operações Base
  //   00000 AND 
  //   00001 OR
  //   00010 NAND
  //   00011 XOR
  //   00100 Somador Inteiros
  //   00101 Somador Naturais
  //   00110 Subtrator
  //   00111 Deslocamento Esquerda
  //   01000 Deslocamento Direita
  //   01001 Deslocamento Direita com Sinal
  //   01010 Rotação Esquerda
  //   01011 Rotação Direita
  //   01100 Menor que
  //   01101 JUMP
  //   01110 BEQ
  //   01111 BNQ
  //   Operações I
  //   10000 AND
  //   10001 OR
  //   10010 NAND
  //   10011 XOR
  //   10100 Somador Inteiros
  //   10101 Somador Naturais
  //   10110 Subtrator
  //   10111 Deslocamento Esquerda
  //   11000 Deslocamento Direita
  //   11001 Deslocamento Direita com Sinal
  //   11010 Rotação Esquerda
  //   11011 Rotação Direita
  //   11100  Menor que
endmodule
